// Logisim project brainfuck_machine.circ as structural Verilog
module main (
  input  CONTROL_RESET,
  input  CONTROL_CLOCK,
  input  CONTROL_ENABLE,
  input  WRITE_DATA,
  input  WRITE_CLOCK,
  input  WRITE_ENABLE,
  output OUTPUT_READY,
  output AWAITING_INPUT,
  output [7:0] ROM_DATA,
  output ROM_CHIP_ENABLE,
  output ROM_WRITE_ENABLE
);

  wire and_1_out, and_2_out, and_3_out, and_4_out, and_5_out, and_6_out, and_7_out, and_8_out, and_9_out,
       and_10_out, and_11_out, and_12_out, and_13_out, and_14_out, clock_1_out, comparator_1_eq,
       comparator_2_eq, comparator_3_eq, comparator_4_eq, comparator_5_eq, comparator_6_eq, comparator_7_eq,
       comparator_8_eq, comparator_9_eq, comparator_10_eq, comparator_11_eq, comparator_12_eq,
       controlled_buffer_1_out, controlled_buffer_3_out, controlled_buffer_6_out, controlled_buffer_20_out,
       d_ff_1_qn, EXT_RESET_out, j_k_ff_1_q, j_k_ff_2_q, j_k_ff_2_qn, j_k_ff_3_q, j_k_ff_3_qn, j_k_ff_4_qn,
       j_k_ff_5_q, j_k_ff_5_qn, monostable_1_pulse, monostable_2_pulse, monostable_3_pulse,
       monostable_4_pulse, monostable_5_pulse, monostable_6_pulse, nor_1_out, nor_2_out, nor_3_out,
       nor_4_out, not_1_out, not_2_out, not_3_out, not_4_out, not_5_out, not_6_out, not_7_out, not_8_out,
       not_9_out, not_10_out, not_11_out, not_12_out, or_1_out, or_2_out, or_3_out, or_4_out, or_5_out,
       or_7_out, or_8_out, or_9_out, RESET_out, s_r_ff_1_q, s_r_ff_1_qn, slow_clock_1_out_2, STARTUP_q,
       TURTLE_p2;
  wire [2:2] OUTPUT_CONFIRMED_out;
  wire [3:0] counter_1_q;
  wire [6:0] bit_extender_2_out, keyboard_1_data;
  wire [7:0] adder_1_out, controlled_buffer_11_out, controlled_buffer_14_out, controlled_buffer_18_out,
       R_IN_q, R_OUT_q, ram_1_data, register_1_q, register_2_q, rom_1_data, subtractor_1_out, undriven;
  wire [8:0] PUSH_INPUT_out;
  wire [14:0] adder_2_out, counter_2_q, counter_3_q, counter_4_q, Jump_Snapshot_q, ram_2_data;

  Button RESET (.out(RESET_out));
  // Switch TURTLE: pin names not known; wires that end beside it: 1'b1, TURTLE_p2
  Pull_Resistor pull_resistor_1 (.node(CONTROL_RESET));
  assign controlled_buffer_1_out = CONTROL_ENABLE ? CONTROL_RESET : 1'bz;  // Controlled_Buffer controlled_buffer_1
  Pull_Resistor pull_resistor_2 (.node(CONTROL_CLOCK));
  Pull_Resistor pull_resistor_3 (.node(CONTROL_ENABLE));
  not not_1 (not_1_out, CONTROL_ENABLE);
  or or_1 (or_1_out, or_4_out, RESET_out);
  Pull_Resistor pull_resistor_4 (.node(TURTLE_p2));
  Pull_Resistor pull_resistor_5 (.node(WRITE_CLOCK));
  Pull_Resistor pull_resistor_6 (.node(WRITE_ENABLE));
  assign controlled_buffer_1_out = not_1_out ? or_1_out : 1'bz;  // Controlled_Buffer controlled_buffer_2
  Pull_Resistor pull_resistor_7 (.node(WRITE_DATA));
  Clock clock_1 (.out(clock_1_out));
  slow_clock slow_clock_1 (.RESET(controlled_buffer_1_out), .out_2(slow_clock_1_out_2));
  // Shift_Register shift_register_1: pin names not known; wires that end beside it: controlled_buffer_1_out, WRITE_ENABLE, WRITE_CLOCK, WRITE_DATA
  not not_2 (not_2_out, WRITE_ENABLE);
  D_Flip_Flop STARTUP (.D(1'b1), .clk(s_r_ff_1_q), .Q(STARTUP_q), .reset(controlled_buffer_1_out));  // open: Qn, preset
  D_Flip_Flop d_ff_1 (
    .D(STARTUP_q), .clk(s_r_ff_1_q), .Qn(d_ff_1_qn), .reset(controlled_buffer_1_out));  // open: Q, preset
  or or_2 (or_2_out, CONTROL_ENABLE, WRITE_ENABLE);
  monostable monostable_1 (.WAVE(WRITE_ENABLE), .PULSE(monostable_1_pulse));
  monostable monostable_2 (.WAVE(not_2_out), .PULSE(monostable_2_pulse));
  or or_3 (or_3_out, TURTLE_p2, or_2_out);
  not not_3 (not_3_out, or_3_out);
  not not_4 (not_4_out, or_2_out);
  not not_5 (not_5_out, WRITE_ENABLE);
  or or_4 (or_4_out, monostable_1_pulse, monostable_2_pulse);
  and and_1 (and_1_out, not_4_out, TURTLE_p2);
  and and_2 (and_2_out, not_5_out, CONTROL_ENABLE);
  Counter #(.max('hf), .width(4)) counter_1 (
    .clr(controlled_buffer_1_out), .load(comparator_1_eq), .count(WRITE_ENABLE), .clk(WRITE_CLOCK),
    .D(4'b0001), .Q(counter_1_q));  // open: up, carry
  nor nor_1 (nor_1_out, comparator_10_eq, d_ff_1_qn, j_k_ff_2_q, AWAITING_INPUT);
  nor nor_2 (nor_2_out, d_ff_1_qn, j_k_ff_2_q, and_12_out, j_k_ff_5_q);
  assign controlled_buffer_3_out = not_3_out ? clock_1_out : 1'bz;  // Controlled_Buffer controlled_buffer_3
  assign controlled_buffer_3_out = and_1_out ? slow_clock_1_out_2 : 1'bz;  // Controlled_Buffer controlled_buffer_4
  assign controlled_buffer_3_out = and_2_out ? CONTROL_CLOCK : 1'bz;  // Controlled_Buffer controlled_buffer_5
  not not_6 (not_6_out, WRITE_CLOCK);
  assign controlled_buffer_6_out = not_2_out ? s_r_ff_1_q : 1'bz;  // Controlled_Buffer controlled_buffer_6
  assign controlled_buffer_6_out = WRITE_ENABLE ? WRITE_CLOCK : 1'bz;  // Controlled_Buffer controlled_buffer_7
  Counter #(.max('h7fff), .width(15)) counter_2 (
    .clr(controlled_buffer_1_out), .load(and_11_out), .count(or_5_out), .clk(controlled_buffer_6_out),
    .D(ram_2_data), .Q(counter_2_q));  // open: up, carry
  or or_5 (or_5_out, comparator_1_eq, nor_1_out);
  Counter #(.max('h7fff), .trigger("falling"), .width(15)) counter_3 (
    .clr(controlled_buffer_1_out), .up(comparator_2_eq), .count(and_4_out), .clk(s_r_ff_1_q), .Q(counter_3_q));  // open: load, D, carry
  Counter #(.max('h7fff), .trigger("falling"), .width(15)) counter_4 (
    .clr(controlled_buffer_1_out), .up(comparator_8_eq), .count(or_9_out), .clk(s_r_ff_1_q), .Q(counter_4_q));  // open: load, D, carry
  not not_7 (not_7_out, controlled_buffer_3_out);
  assign ROM_WRITE_ENABLE = WRITE_ENABLE ? not_6_out : 1'bz;  // Controlled_Buffer controlled_buffer_8
  S_R_Flip_Flop s_r_ff_1 (.Q(s_r_ff_1_q), .reset(nor_4_out), .Qn(s_r_ff_1_qn), .preset(nor_3_out));  // open: S, R, clk
  nor nor_3 (nor_3_out, not_7_out, monostable_4_pulse);
  nor nor_4 (nor_4_out, controlled_buffer_3_out, monostable_3_pulse);
  monostable monostable_3 (.WAVE(s_r_ff_1_q), .PULSE(monostable_3_pulse));
  monostable monostable_4 (.WAVE(s_r_ff_1_qn), .PULSE(monostable_4_pulse));
  Comparator #(.width(4)) comparator_1 (.a(counter_1_q), .b(4'b1000), .eq(comparator_1_eq));  // open: gt, lt
  ROM #(.addrWidth(15)) rom_1 (.addr(counter_2_q), .data(rom_1_data));
  RAM #(.addrWidth(15), .asyncread("true"), .clearpin("true"), .databus("bidir"), .trigger("falling")) ram_1 (
    .addr(counter_3_q), .we(and_3_out), .oe(not_8_out), .clk(s_r_ff_1_q), .data(ram_1_data),
    .clr(controlled_buffer_1_out));
  not not_8 (not_8_out, and_3_out);
  not not_9 (not_9_out, and_10_out);
  or or_6 (ROM_CHIP_ENABLE, comparator_1_eq, not_10_out);
  not not_10 (not_10_out, WRITE_ENABLE);
  RAM #(.addrWidth(15), .asyncread("true"), .clearpin("true"), .dataWidth(15), .databus("bidir"), .trigger("falling")) ram_2 (
    .addr(counter_4_q), .we(and_10_out), .oe(not_9_out), .clk(s_r_ff_1_q), .data(ram_2_data),
    .clr(controlled_buffer_1_out));
  assign ROM_DATA = WRITE_ENABLE ? undriven : 8'bz;  // Controlled_Buffer controlled_buffer_9
  assign ROM_DATA = not_2_out ? rom_1_data : 8'bz;  // Controlled_Buffer controlled_buffer_10
  assign controlled_buffer_11_out = j_k_ff_5_q ? {8{1'b0}} : 8'bz;  // Controlled_Buffer controlled_buffer_11
  not not_11 (not_11_out, j_k_ff_5_q);
  assign controlled_buffer_11_out = not_11_out ? ROM_DATA : 8'bz;  // Controlled_Buffer controlled_buffer_12
  Adder adder_1 (.a(ram_1_data), .b(8'h1), .out(adder_1_out));  // open: cin, cout
  Subtractor subtractor_1 (.a(ram_1_data), .b(8'h1), .out(subtractor_1_out));  // open: bin, bout
  assign ram_2_data = and_10_out ? counter_2_q : 15'bz;  // Controlled_Buffer controlled_buffer_13
  Comparator comparator_2 (.a(controlled_buffer_11_out), .b(8'h3e), .eq(comparator_2_eq));  // open: gt, lt
  Comparator comparator_3 (.a(controlled_buffer_11_out), .b(8'h3c), .eq(comparator_3_eq));  // open: gt, lt
  Comparator comparator_4 (.a(controlled_buffer_11_out), .b(8'h2b), .eq(comparator_4_eq));  // open: gt, lt
  Comparator comparator_5 (.a(controlled_buffer_11_out), .b(8'h2d), .eq(comparator_5_eq));  // open: gt, lt
  Comparator comparator_6 (.a(controlled_buffer_11_out), .b(8'h2e), .eq(comparator_6_eq));  // open: gt, lt
  Comparator comparator_7 (.a(controlled_buffer_11_out), .b(8'h2c), .eq(comparator_7_eq));  // open: gt, lt
  Comparator comparator_8 (.a(ROM_DATA), .b(8'h5b), .eq(comparator_8_eq));  // open: gt, lt
  Comparator comparator_9 (.a(ROM_DATA), .b(8'h5d), .eq(comparator_9_eq));  // open: gt, lt
  Comparator comparator_10 (.a(ROM_DATA), .b({8{1'b0}}), .eq(comparator_10_eq));  // open: gt, lt
  Register register_1 (.D(adder_1_out), .clk(s_r_ff_1_q), .Q(register_1_q), .clr(controlled_buffer_1_out));  // open: en
  Register register_2 (
    .D(subtractor_1_out), .clk(s_r_ff_1_q), .Q(register_2_q), .clr(controlled_buffer_1_out));  // open: en
  or or_7 (or_7_out, comparator_4_eq, comparator_5_eq, comparator_7_eq);
  assign controlled_buffer_14_out = comparator_7_eq ? R_IN_q : 8'bz;  // Controlled_Buffer controlled_buffer_14
  assign controlled_buffer_14_out = comparator_4_eq ? register_1_q : 8'bz;  // Controlled_Buffer controlled_buffer_15
  assign controlled_buffer_14_out = comparator_5_eq ? register_2_q : 8'bz;  // Controlled_Buffer controlled_buffer_16
  and and_3 (and_3_out, or_7_out, nor_2_out);
  assign ram_1_data = and_3_out ? controlled_buffer_14_out : 8'bz;  // Controlled_Buffer controlled_buffer_17
  or or_8 (or_8_out, comparator_2_eq, comparator_3_eq);
  and and_4 (and_4_out, or_8_out, nor_2_out);
  and and_5 (and_5_out, j_k_ff_2_q, monostable_5_pulse);
  monostable monostable_5 (.WAVE(OUTPUT_CONFIRMED_out[2]), .PULSE(monostable_5_pulse));
  or or_9 (or_9_out, comparator_9_eq, comparator_8_eq);
  J_K_Flip_Flop #(.trigger("falling")) j_k_ff_1 (
    .J(1'b0), .K(j_k_ff_1_q), .clk(s_r_ff_1_q), .Q(j_k_ff_1_q), .preset(and_5_out),
    .reset(controlled_buffer_1_out));  // open: Qn
  and and_6 (and_6_out, j_k_ff_2_q, j_k_ff_1_q);
  and and_7 (and_7_out, j_k_ff_2_qn, comparator_6_eq);
  Register #(.trigger("falling")) R_OUT (
    .D(ram_1_data), .en(and_7_out), .clk(s_r_ff_1_q), .Q(R_OUT_q), .clr(controlled_buffer_1_out));
  Register R_IN (
    .D(controlled_buffer_18_out), .en(AWAITING_INPUT), .clk(controlled_buffer_20_out), .Q(R_IN_q),
    .clr(controlled_buffer_1_out));
  and and_8 (and_8_out, AWAITING_INPUT, j_k_ff_3_q);
  and and_9 (and_9_out, comparator_7_eq, j_k_ff_4_qn);
  Comparator comparator_11 (.a(ram_1_data), .b({8{1'b0}}), .eq(comparator_11_eq));  // open: gt, lt
  J_K_Flip_Flop #(.trigger("falling")) j_k_ff_2 (
    .J(and_7_out), .K(and_6_out), .clk(s_r_ff_1_q), .Q(j_k_ff_2_q), .Qn(j_k_ff_2_qn),
    .reset(controlled_buffer_1_out));  // open: preset
  monostable monostable_6 (.WAVE(controlled_buffer_20_out), .PULSE(monostable_6_pulse));
  J_K_Flip_Flop #(.trigger("falling")) j_k_ff_3 (
    .J(1'b0), .K(and_8_out), .clk(s_r_ff_1_q), .Q(j_k_ff_3_q), .Qn(j_k_ff_3_qn), .preset(monostable_6_pulse),
    .reset(controlled_buffer_1_out));
  J_K_Flip_Flop #(.trigger("falling")) j_k_ff_4 (
    .J(and_9_out), .K(and_8_out), .clk(s_r_ff_1_q), .Q(AWAITING_INPUT), .Qn(j_k_ff_4_qn),
    .reset(controlled_buffer_1_out));  // open: preset
  not not_12 (not_12_out, comparator_11_eq);
  and and_10 (and_10_out, comparator_8_eq, not_12_out);
  and and_11 (and_11_out, not_12_out, comparator_9_eq);
  assign controlled_buffer_18_out = comparator_6_eq ? R_OUT_q : 8'bz;  // Controlled_Buffer controlled_buffer_18
  and and_12 (and_12_out, AWAITING_INPUT, j_k_ff_3_qn);
  and and_13 (and_13_out, j_k_ff_5_qn, comparator_11_eq, comparator_8_eq);
  assign OUTPUT_READY = comparator_6_eq ? j_k_ff_2_q : 1'bz;  // Controlled_Buffer controlled_buffer_19
  and and_14 (and_14_out, j_k_ff_5_q, comparator_9_eq, comparator_12_eq);
  J_K_Flip_Flop #(.trigger("falling")) j_k_ff_5 (
    .J(and_13_out), .K(and_14_out), .clk(s_r_ff_1_q), .Q(j_k_ff_5_q), .Qn(j_k_ff_5_qn),
    .reset(controlled_buffer_1_out));  // open: preset
  Adder #(.width(15)) adder_2 (.a(counter_4_q), .b(15'h1), .out(adder_2_out));  // open: cin, cout
  assign controlled_buffer_20_out = AWAITING_INPUT ? OUTPUT_READY : 1'bz;  // Controlled_Buffer controlled_buffer_20
  Register #(.trigger("falling"), .width(15)) Jump_Snapshot (
    .D(adder_2_out), .en(and_13_out), .clk(s_r_ff_1_q), .Q(Jump_Snapshot_q), .clr(controlled_buffer_1_out));
  Comparator #(.width(15)) comparator_12 (.a(Jump_Snapshot_q), .b(counter_4_q), .eq(comparator_12_eq));  // open: gt, lt
  assign {controlled_buffer_18_out, OUTPUT_READY} = AWAITING_INPUT ? PUSH_INPUT_out : 9'bz;  // Controlled_Buffer controlled_buffer_21
  Keyboard keyboard_1 (.clk(PUSH_INPUT_out[0]), .clr(EXT_RESET_out), .data(keyboard_1_data));  // open: re, avail
  Button PUSH_INPUT (.out(PUSH_INPUT_out[0]));
  Button OUTPUT_CONFIRMED (.out(OUTPUT_CONFIRMED_out[2]));
  assign PUSH_INPUT_out[8:1] = {{1{1'b0}}, keyboard_1_data};  // Bit_Extender bit_extender_1
  Bit_Extender #(.out_width(7), .\type ("zero")) bit_extender_2 (
    .in(controlled_buffer_18_out), .out(bit_extender_2_out));
  TTY tty_1 (.data(bit_extender_2_out), .clk(OUTPUT_CONFIRMED_out[2]), .we(OUTPUT_READY), .clr(EXT_RESET_out));
  Button EXT_RESET (.out(EXT_RESET_out));

  // Notes on the sheet:
  //   clock filter
  //   contents of rom_1 (hex, n*v repeats v):
  //   3e 2c 10*2d 5b 38*2d 3e 10*2b 3c 3c 5b 2d 3e 3e 3e 2b 3c 3c 3c 5d 3e 3e 5b 2d 3e 5b 2d 3e 2b 3c 3c d
  //   a 3c 3c 2b 3e 3e 3e 5d 3e 5b 2d 3c 2b 3e 5d 3c 3c 5d 3e 5b 2d 5d 3c 3c 5b 2d 3c 2b 3e 5d 2c 10*2d 5d
  //   2b 3c 2d 5b 2b 3e 2b 3c 5b 2d 3e 3e 2b 3e 2b 3c 3c 3c 5d 3e 3e 3e 5b 2d 3c 3c 3c 2b 3e 3e 3e 5d 3e
  //   2b 5b 5b 2d 3c 2b 3c 2d 3c 2d 5b d a 2d 4*3e 2b 3e 2b 5*3c 5d 5*3e 5b 2d 5*3c 2b 5*3e 5d 3c 5b 3c 2b
  //   3e 5b 2d 5d 5d 3c 5b 2d 3e 2b 3e 2b 3c 3c 5d 3e 3e 5b 2d 3c 3c 2b 3e 3e 5d 3c 5b 5b 2d 5d 3c 2d 3c
  //   3c 5b 2d 3e 3e 3e 2b 3e 2b 4*3c 5d 3e d a 3e 3e 3e 5b 2d 4*3c 2b 4*3e 5d 3c 5b 3c 2b 3e 5b 2d 5d 5d
  //   5d 3c 5d 3c 3c 5b 2d 3e 3e 3e 2b 3e 2b 4*3c 5d 4*3e 5b 2d 4*3c 2b 4*3e 5d 3c 5b 3c 2b 3e 5b 2d 5d 5d
  //   3c 5b 2d 3e 2b 3e 2b 3c 3c 5d 3e 3e 5b 2d 3c 3c 2b 3e d a 3e 5d 3c 5b 3c 3c 5b 2d 3c 3c 2b 3e 3e 5d
  //   3e 3e 5b 2d 5d 5d 3c 5d 2b 3c 3c 3c 5b 2d 4*3e 2b 3e 2b 5*3c 5d 5*3e 5b 2d 5*3c 2b 5*3e 5d 3c 5b 3c
  //   2d 3e 5b 2d 5d 5d 3c 3c 5b 2d 3c 3c 2b 3e 3e 5d 3e 5b 2d 3c 2b 3e d a 5d 3c 5b 2d 3c 3c 3c 5b 3e 3e
  //   2b 3c 5b 2d 3c 2d 3e 3e 3e 2b 3c 3c 5d 3e 3e 5b 2d 3c 3c 2b 3e 3e 5d 3c 3c 3c 5d 3e 3e 5b 2d 3c 3c
  //   2b 3e 3e 5d 3c 5b 2d 3e 2b 3e 2b 3c 3c 5d 3e 3e 5b 2d 3c 3c 2b 3e 3e 5d 2b 5b 3e 10*2b 5b 3c 3c 5b
  //   2d d a 3e 3e 3e 2b 3e 2b 4*3c 5d 4*3e 5b 2d 4*3c 2b 4*3e 5d 3c 5b 3c 3c 3c 2d 3e 3e 3e 5b 2d 5d 5d
  //   3c 2d 5d 3e 3e 3e 2b 4*3c 2d 5d 4*3e 5b 2d 4*3c 2b 4*3e 5d 5*3c 5b 5b 2d 5d 3e 5b 2d 3e 2b 2b 2b d a
  //   7*2b 3c 5d 3e 5b 2d 3c 2b 3e 5d 3c 3c 3c 5b 2d 3e 2b 3e 3e 2b 3c 3c 3c 5d 3e 3e 3e 5b 2d 3c 3c 3c 2b
  //   3e 3e 3e 5d 3c 5b 3e 10*2b 5b 3c 3c 5b 2d 3e 3e 3e 2b 3e 2b 4*3c 5d 4*3e 5b 2d 4*3c 2b 3e 3e d a 3e
  //   3e 5d 3c 5b 3c 3c 3c 2d 3e 3e 3e 5b 2d 5d 5d 3c 2d 5d 3e 3e 3e 2b 4*3c 2d 5d 4*3e 5b 2d 4*3c 2b 4*3e
  //   5d 5*3c 5d 3c 5b 2d 3e 2b 3e 3e 2b 3c 3c 3c 5d 3e 3e 3e 5b 2d 3c 3c 3c 2b 3e 3e 3e 5d 3c 2d 5b 2b 3e
  //   3e 3e 2b 5b d a 5b 2d 3c 3c 2b 3c 2d 3c 2d 3e 5b 2d 4*3e 2b 3e 2b 5*3c 5d 5*3e 5b 2d 5*3c 2b 5*3e 5d
  //   3c 5b 3c 2b 3e 5b 2d 5d 5d 3c 5b 2d 3e 2b 3e 2b 3c 3c 5d 3e 3e 5b 2d 3c 3c 2b 3e 3e 5d 3c 5b 5b 2d
  //   5d 3c 2d 4*3c 5b d a 2d 5*3e 2b 3e 2b 6*3c 5d 6*3e 5b 2d 6*3c 2b 6*3e 5d 3c 5b 3c 2b 3e 5b 2d 5d 5d
  //   5d 3c 5d 2b 3c 3c 3c 5b 2d 4*3e 2b 3e 2b 5*3c 5d 5*3e 5b 2d 5*3c 2b 3e 3e 3e d a 3e 3e 5d 3c 5b 5b
  //   2d 5d 3c 2d 3e 5d 3c 5b 2d 3e 2b 3e 2b 3c 3c 5d 3e 3e 5b 2d 3c 3c 2b 3e 3e 5d 3c 5b 5b 2d 5d 3c 3c
  //   2b 3c 5b 2d 3c 2b 3e 5d 3e 3e 3e 5d 3c 5d 3c 31*2b d a 17*2b 2e 5b 2d 5d 3c 5b 2d 3c 2b 3c 2b 3e 3e
  //   5d 3c 5b 10*2d 3e 2b 3c 5d 3e 5b 2d 3c 2b 3e 5d 3c 2d 5d 3c 27*2b d a 21*2b 2e 5b 2d 5d 10*2b 2e 5b
  //   2d 5d 3c 3c 5b 2d 3e 3e 2b 3e 2b 3c 3c 3c 5d 3e 3e 3e 5b 2d 3c 3c 3c 2b 3e 3e 3e 5d 3e 2b 5b 5b 2d
  //   3c 2b 3c 2d 3c 2d 5b 2d 4*3e 2b 3e 2b d a 5*3c 5d 5*3e 5b 2d 5*3c 2b 5*3e 5d 3c 5b 3c 2b 3e 5b 2d 5d
  //   5d 3c 5b 2d 3e 2b 3e 2b 3c 3c 5d 3e 3e 5b 2d 3c 3c 2b 3e 3e 5d 3c 5b 5b 2d 5d 3c 2d 3c 3c 5b 2d 3e
  //   3e 3e 2b 3e 2b 4*3c 5d 4*3e 5b 2d 3c 3c 3c d a 3c 2b 4*3e 5d 3c 5b 3c 2b 3e 5b 2d 5d 5d 5d 3c 5d 3c
  //   3c 5b 2d 3e 3e 3e 2b 3e 2b 4*3c 5d 4*3e 5b 2d 4*3c 2b 4*3e 5d 3c 5b 3c 2b 3e 5b 2d 5d 5d 3c 5b 2d 3e
  //   2b 3e 2b 3c 3c 5d 3e 3e 5b 2d 3c 3c 2b 3e 3e 5d 3c 5b 3c 3c 5b 2d d a 3c 3c 2b 3e 3e 5d 3e 3e 5b 2d
  //   5d 5d 3c 5d 2b 3c 3c 3c 5b 2d 4*3e 2b 3e 2b 5*3c 5d 5*3e 5b 2d 5*3c 2b 5*3e 5d 3c 5b 3c 2d 3e 5b 2d
  //   5d 5d 3c 3c 5b 2d 3c 3c 2b 3e 3e 5d 3e 5b 2d 3c 2b 3e 5d 3c 5d 3c 3c 3c 2d 5d
  //   >
  //   <
  //   +
  //   -
  //   .
  //   ,
  //   [
  //   ]
  //   \0
  //   State OUTPUT
  //   OE
  //   IE
  //   State INPUT
  //   State JUMPING
endmodule

module monostable (
  input  WAVE,
  output PULSE
);

  wire not_1_out;

  not not_1 (not_1_out, WAVE);
  and and_1 (PULSE, not_1_out, WAVE);
endmodule

module slow_clock (
  input  RESET,
  output out_2
);

  wire clock_1_out, clock_2_out, counter_1_carry;

  Clock clock_1 (.out(clock_1_out));
  Counter #(.max('h1f3), .width(10)) counter_1 (
    .clr(RESET), .clk(clock_1_out), .carry(counter_1_carry));  // open: load, up, count, D, Q
  T_Flip_Flop t_ff_1 (.T(counter_1_carry), .clk(clock_2_out), .Q(out_2), .reset(RESET));  // open: Qn, preset
  Clock clock_2 (.out(clock_2_out));
endmodule
